# Fritzing sketch Stepper_Control_PCB (saved by Fritzing 0.9.3b)
circuit board: 5.7cm x 5.3cm
breadboards: 1

parts:
  M2 = Stepper Motor - Bipolar
  JP2 = Header 5 [package=1x05-1mm]
  JP3 = Header 4 [package=1x04-1mm-ra]
  R2 = Trimmer Potentiometer [maximum_resistance=10kΩ package=THT]
  IC1 = H-Bridge [package=THT]

nets:
  N1: M2.A, IC1.1Y
  N2: M2.C, IC1.2Y
  N3: M2.B, IC1.4Y
  N4: M2.D, IC1.3Y
  N5: JP2.1, IC1.4A
  N6: JP2.2, IC1.3A
  N7: JP2.3, IC1.2A
  N8: JP2.4, IC1.1A
  N9: JP2.5, R2.wiper
  N10: JP3.2, IC1.VCC2
  N11: JP3.3, R2.leg2, IC1.1_2EN, IC1.3_4EN, IC1.VCC1
  GND1: JP3.4, R2.leg1, IC1.GND1, IC1.GND2, IC1.GND3, IC1.GND4
